# Fritzing sketch Skypaw_electronics (saved by Fritzing 0.9.3b)
breadboards: 1

parts:
  Pico_H1 = Raspberry Pi Pico H
  Part1 = Adafruit PCA9685 PWM/Servo Breakout [part_number=815]
  SERVO1 = Tower Pro SG90 servo [part_number=101246]
  SERVO2 = Tower Pro SG90 servo [part_number=101246]
  hc-sr2 = hc-sr04
  hc-sr3 = hc-sr04
  Part2 = BH1750 digital light sensor
  SERVO3 = Tower Pro SG90 servo [part_number=101246]
  SERVO4 = Tower Pro SG90 servo [part_number=101246]
  SERVO5 = Tower Pro SG90 servo [part_number=101246]
  SERVO6 = Tower Pro SG90 servo [part_number=101246]
  SERVO7 = Tower Pro SG90 servo [part_number=101246]
  SERVO8 = Tower Pro SG90 servo [part_number=101246]
  SERVO9 = Tower Pro SG90 servo [part_number=101246]
  SERVO10 = Tower Pro SG90 servo [part_number=101246]
  VCC1 = Battery
  VCC2 = Battery

nets:
  VCC: Pico_H1.VBUS, Part1.VCC, hc-sr2.VCC, hc-sr3.VCC, VCC2.+
  GND: Pico_H1.GND, Part1.GND, SERVO1.GND, SERVO2.GND, hc-sr2.GND, hc-sr3.GND, Part2.GND, SERVO3.GND, SERVO4.GND, SERVO5.GND, SERVO6.GND, SERVO7.GND, SERVO8.GND, SERVO9.GND, SERVO10.GND, VCC1.-
  3V3: Pico_H1.3V3, Part2.VCC
  N1: Pico_H1.GP21, hc-sr3.Trig
  N2: Pico_H1.GP20, hc-sr3.Echo
  N3: Pico_H1.GP19, hc-sr2.Trig
  N4: Pico_H1.GP18, hc-sr2.Echo
  N5: Pico_H1.GP1, Part1.SCL, Part2.SCL
  N6: Pico_H1.GP0, Part1.SDA, Part2.SDA
  N7: Part1.PWM4, SERVO1.Signal
  +5V: Part1.5.0V, SERVO1.+5V, SERVO2.+5V, SERVO3.+5V, SERVO4.+5V, SERVO5.+5V, SERVO6.+5V, SERVO7.+5V, SERVO8.+5V, SERVO9.+5V, SERVO10.+5V
  N8: Part1.PWM3, SERVO2.Signal
  N9: Part1.PWM2, SERVO9.Signal
  N10: Part1.PWM1, SERVO10.Signal
  N11: Part1.PWM0, SERVO8.Signal
  N12: Part1.PWM15, SERVO3.Signal
  N13: Part1.PWM14, SERVO7.Signal
  N14: Part1.PWM13, SERVO4.Signal
  N15: Part1.PWM12, SERVO6.Signal
  N16: Part1.PWM11, SERVO5.Signal
  N17: VCC1.+, VCC2.-

custom parts:
  Raspberry Pi Pico H: Raspberry Pi Pico H. Based around the RP2040 microcontroller the Pico H is a low cost microcontroller device bringing Raspberry Pi quality, cost, and easy of use to the microcontroller space.
  Adafruit PCA9685 PWM/Servo Breakout: Using only two pins, control 16 free-running PWM outputs! I2C-controlled PWM driver with a built in clock. Unlike the TLC5940 family, you do not need to continuously send it signal tying up your microcontroller, its completely free running! 5V compliant, which means you can control it from a 3.3V microcontroller and still safely drive up to 6V outputs (this is good for when you want to control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
  Tower Pro SG90 servo: Original file by John De Cristofaro http://www.adafruit.com/products/1449 Adafruit Feedback Servo (Small) Edited by: e-radionica.com 28/9/2015
  BH1750 digital light sensor: BH1750 digital light sensor SKU: 101222
